# Fritzing sketch sparkcopter (saved by Fritzing 0.9.1b)
breadboards: 1

parts:
  Spark_Core = Spark Core (v1.0)
  MPU-6050 = MPU-6050 Board GY-521 [form="♀ (female)" package=THT]
  Q-FL = NPN-Transistor [package="TO92 [THT]"]
  M-FL = DC Motor
  D-FL = Diode [package=diode-1n4148]
  3_7v_LIPO_Battery = LIPO-110mAh [package=lipo-110]
  Q-FR = NPN-Transistor [package="TO92 [THT]"]
  Q-BR = NPN-Transistor [package="TO92 [THT]"]
  M-FR = DC Motor
  M-BL = DC Motor
  M-BR = DC Motor
  Q-BL = NPN-Transistor [package="TO92 [THT]"]
  D-FR = Diode [package=diode-1n4148]
  D-BL = Diode [package=diode-1n4148]
  D-BR = Diode [package=diode-1n4148]

nets:
  N1: Spark_Core.A0, Q-BL.B
  N2: Spark_Core.A1, Q-BR.B
  N3: Spark_Core.A4, Q-FR.B
  N4: Spark_Core.A5, Q-FL.B
  GND: Spark_Core.GND, MPU-6050.pin2, Q-FL.E, D-FL.A, 3_7v_LIPO_Battery.-, Q-FR.E, Q-BR.E, Q-BL.E, D-FR.A, D-BL.A, D-BR.A
  N5: Spark_Core.VIN, M-FL.pin_1, 3_7v_LIPO_Battery.+, M-FR.pin_1, M-BL.pin_1, M-BR.pin_1
  N6: Spark_Core.D0, MPU-6050.pin4
  N7: Spark_Core.D1, MPU-6050.pin3
  N8: Spark_Core.3V3, MPU-6050.pin1
  N9: Q-FL.C, M-FL.pin_2, D-FL.C
  N10: Q-FR.C, M-FR.pin_2, D-FR.C
  N11: Q-BR.C, M-BR.pin_2, D-BR.C
  N12: M-BL.pin_2, Q-BL.C, D-BL.C

custom parts:
  MPU-6050 Board GY-521: Acelerometro y Giroscopio MPU-6050 Board GY-521
